// Logisim project LOGIC gates.circ as structural Verilog: 1 circuit, main circuit main
module main (
);

  wire undriven, undriven_2, undriven_3, undriven_4, undriven_5, undriven_6, undriven_7, undriven_8,
       undriven_9, undriven_10, undriven_11, undriven_12, undriven_13, undriven_14, undriven_15, undriven_16,
       undriven_17, undriven_18, undriven_19, undriven_20, undriven_21, undriven_22, undriven_23,
       undriven_24, undriven_25, undriven_26, undriven_27, undriven_28, undriven_29, undriven_30,
       undriven_31, undriven_32, undriven_33, undriven_34, undriven_35, undriven_36, undriven_37,
       undriven_38, undriven_39, undriven_40, undriven_41, undriven_42, undriven_43, undriven_44,
       undriven_45, undriven_46, undriven_47, undriven_48;
  wire [2:0] and_1_out, or_1_out, xor_1_out;

  Multiplexer #(.select(3), .width(3)) multiplexer_1 (
    .in1(and_1_out), .in4(or_1_out), .in7(xor_1_out));  // open: in0, in2, in3, in5, in6, out, sel, en
  and and_1 (and_1_out[0], undriven, undriven_4);
  or or_1 (or_1_out[0], undriven_2, undriven_5);
  xor xor_1 (xor_1_out[0], undriven_3, undriven_6);
  // AND_Gate and_2 has open pins: in0=undriven_7, in1=undriven_10, out=open
  // OR_Gate or_2 has open pins: in0=undriven_8, in1=undriven_11, out=open
  // XOR_Gate xor_2 has open pins: in0=undriven_9, in1=undriven_12, out=open
  // AND_Gate and_3 has open pins: in0=undriven_19, in1=undriven_22, out=open
  // AND_Gate and_4 has open pins: in0=undriven_13, in1=undriven_16, out=open
  // OR_Gate or_3 has open pins: in0=undriven_14, in1=undriven_17, out=open
  // OR_Gate or_4 has open pins: in0=undriven_20, in1=undriven_23, out=open
  // XOR_Gate xor_3 has open pins: in0=undriven_15, in1=undriven_18, out=open
  // XOR_Gate xor_4 has open pins: in0=undriven_21, in1=undriven_24, out=open
  // AND_Gate and_5 has open pins: in0=undriven_25, in1=undriven_28, out=open
  // OR_Gate or_5 has open pins: in0=undriven_26, in1=undriven_29, out=open
  // XOR_Gate xor_5 has open pins: in0=undriven_27, in1=undriven_30, out=open
  // AND_Gate and_6 has open pins: in0=undriven_37, in1=undriven_40, out=open
  // AND_Gate and_7 has open pins: in0=undriven_31, in1=undriven_34, out=open
  // OR_Gate or_6 has open pins: in0=undriven_32, in1=undriven_35, out=open
  // OR_Gate or_7 has open pins: in0=undriven_38, in1=undriven_41, out=open
  // XOR_Gate xor_6 has open pins: in0=undriven_39, in1=undriven_42, out=open
  // XOR_Gate xor_7 has open pins: in0=undriven_33, in1=undriven_36, out=open
  // AND_Gate and_8 has open pins: in0=undriven_43, in1=undriven_46, out=open
  // OR_Gate or_8 has open pins: in0=undriven_44, in1=undriven_47, out=open
  // XOR_Gate xor_8 has open pins: in0=undriven_45, in1=undriven_48, out=open
  // Pins of 1 and 3 bits meet at or_1_out
  // Pins of 1 and 3 bits meet at and_1_out
  // Pins of 1 and 3 bits meet at xor_1_out

  // Notes on the sheet:
  //   B7
  //   B6
  //   A6
  //   A7
  //   A5
  //   B5
  //   A4
  //   B4
  //   B3
  //   A3
  //   B2
  //   A1
  //   B1
  //   A2
  //   B0
  //   A0
endmodule
