// Logisim project OPCODE.circ as structural Verilog: 1 circuit, main circuit main
module main (
  input  [7:0] in_1,
  input  [7:0] Y,
  input  [7:0] B,
  input  Y_2,
  input  in_5,
  input  in_6,
  input  AND,
  input  OR,
  input  in_9
);

  wire and_1_out, and_2_out, and_5_out, and_6_out, and_7_out, and_8_out, multiplexer_2_out, not_1_out,
       not_2_out, not_3_out, not_4_out, not_5_out, not_6_out, or_1_out, or_2_out, transmission_1_p4,
       transmission_2_p3, transmission_3_p3, undriven, undriven_2, undriven_3, xor_1_out;
  wire [1:0] multiplexer_1_out;
  wire [2:0] and_3_out;

  and and_1 (and_1_out, OR, and_3_out[0]);
  or or_1 (or_1_out, in_5, in_6);
  not not_1 (not_1_out, or_1_out);
  and and_2 (and_2_out, AND, and_3_out[0]);
  and and_3 (and_3_out[0], not_1_out, or_2_out);
  or or_2 (or_2_out, AND, OR);
  xor xor_1 (xor_1_out, in_5, in_6);
  and and_4 (and_3_out[0], in_5, in_6);
  and and_5 (and_5_out, in_9, and_3_out[0]);
  and and_6 (and_6_out, AND, and_3_out[0]);
  and and_7 (and_7_out, OR, and_3_out[0]);
  Multiplexer #(.width(2)) multiplexer_1 (.in0(in_1[1:0]), .in1(Y[1:0]), .out(multiplexer_1_out), .sel(Y_2), .en(Y_2));
  and and_8 (and_8_out, xor_1_out, in_6);
  Multiplexer #(.select(3)) multiplexer_2 (
    .in0(undriven), .in4(undriven_2), .in7(undriven_3), .out(multiplexer_2_out), .sel(and_3_out),
    .en(xor_1_out));  // open: in1, in2, in3, in5, in6
  not not_2 (not_2_out, xor_1_out);
  // Transmission_Gate transmission_1: pin names not known; wires that end beside it: multiplexer_2_out, not_2_out, multiplexer_1_out, transmission_1_p4, xor_1_out
  not not_3 (not_3_out, and_3_out[0]);
  // Transmission_Gate transmission_2: pin names not known; wires that end beside it: not_3_out, multiplexer_1_out, transmission_2_p3, and_3_out
  not not_4 (not_4_out, and_3_out[0]);
  // Transmission_Gate transmission_3: pin names not known; wires that end beside it: not_4_out, multiplexer_1_out, transmission_3_p3, and_3_out
  not not_5 (not_5_out, xor_1_out);
  // Transmission_Gate transmission_4: pin names not known; wires that end beside it: not_5_out, B, transmission_1_p4, xor_1_out
  not not_6 (not_6_out, and_3_out[0]);
  // Transmission_Gate transmission_5: pin names not known; wires that end beside it: not_6_out, B, transmission_3_p3, and_3_out
  // Pins of 1 and 3 bits meet at and_3_out
  // Pins of 2 and 8 bits meet at in_1
  // Pins of 2 and 8 bits meet at Y

  // Notes on the sheet:
  //   OR select bit
  //   LOGIC
  //   XOR if both
  //   LOGIC BLOCK
  //   AND select bit
  //   SUB/ADD
  //   SHIFTER
  //   LOGIC is on just if ADD/SUB/SHOFTER is off
  //   A
  //   if shifter>>send shift bits
  //   SHIFTER BLOCK
  //    8 MUX
  //   SUB/ADD BLOCK
  //   3X3 MUX
  //   IF_SUB
  //   ADD/SUB RESULT
  //   SHIFTER RESULT
  //   LOGIC RESULT
  //   8 TG
  //   8 TG
  //   8 TG
  //   8 TG
  //   8 TG
endmodule
