// Logisim project right shift 4.circ as structural Verilog: 1 circuit, main circuit main
module main (
);

  wire undriven, undriven_2, undriven_3;
  wire [1:0] multiplexer_1_out, multiplexer_2_out, multiplexer_3_out, multiplexer_4_out, multiplexer_5_out,
       multiplexer_6_out, multiplexer_7_out, multiplexer_8_out, multiplexer_9_out, multiplexer_10_out,
       multiplexer_11_out, multiplexer_12_out, multiplexer_13_out, multiplexer_14_out, multiplexer_15_out,
       multiplexer_16_out, multiplexer_17_out, multiplexer_18_out, multiplexer_19_out, multiplexer_20_out,
       multiplexer_21_out, undriven_4, undriven_5, undriven_6, undriven_7, undriven_8, undriven_9,
       undriven_10, undriven_11;

  Multiplexer #(.width(2), .disabled(0), .enable("false")) multiplexer_1 (
    .in0(undriven_4), .in1(undriven_5), .out(multiplexer_1_out), .sel(undriven));
  Multiplexer #(.width(2), .disabled(0), .enable("false")) multiplexer_2 (
    .in0(undriven_4), .in1(multiplexer_1_out), .out(multiplexer_2_out), .sel(undriven_2));
  Multiplexer #(.width(2), .disabled(0), .enable("false")) multiplexer_3 (
    .in0(undriven_4), .in1(multiplexer_2_out), .out(multiplexer_3_out), .sel(undriven_3));
  Multiplexer #(.width(2), .enable("false")) multiplexer_4 (
    .in0(undriven_4), .in1(undriven_6), .out(multiplexer_4_out), .sel(undriven));
  Multiplexer #(.width(2), .enable("false")) multiplexer_5 (
    .in0(undriven_4), .in1(multiplexer_4_out), .out(multiplexer_5_out), .sel(undriven_2));
  Multiplexer #(.width(2), .enable("false")) multiplexer_6 (
    .in0(multiplexer_2_out), .in1(multiplexer_5_out), .out(multiplexer_6_out), .sel(undriven_3));
  Multiplexer #(.width(2), .disabled(0), .enable("false")) multiplexer_7 (
    .in0(undriven_4), .in1(undriven_7), .out(multiplexer_7_out), .sel(undriven));
  Multiplexer #(.width(2), .disabled(0), .enable("false")) multiplexer_8 (
    .in0(multiplexer_1_out), .in1(multiplexer_7_out), .out(multiplexer_8_out), .sel(undriven_2));
  Multiplexer #(.width(2), .disabled(0), .enable("false")) multiplexer_9 (
    .in0(multiplexer_5_out), .in1(multiplexer_8_out), .out(multiplexer_9_out), .sel(undriven_3));
  Multiplexer #(.width(2), .enable("false")) multiplexer_10 (
    .in0(undriven_4), .in1(undriven_8), .out(multiplexer_10_out), .sel(undriven));
  Multiplexer #(.width(2), .enable("false")) multiplexer_11 (
    .in0(multiplexer_4_out), .in1(multiplexer_10_out), .out(multiplexer_11_out), .sel(undriven_2));
  Multiplexer #(.width(2), .disabled(0), .enable("false")) multiplexer_12 (
    .in0(multiplexer_11_out), .in1(multiplexer_15_out), .out(multiplexer_12_out), .sel(undriven_3));
  Multiplexer #(.width(2), .enable("false")) multiplexer_13 (
    .in0(multiplexer_8_out), .in1(multiplexer_11_out), .out(multiplexer_13_out), .sel(undriven_3));
  Multiplexer #(.width(2), .disabled(0), .enable("false")) multiplexer_14 (
    .in0(undriven_5), .in1(undriven_9), .out(multiplexer_14_out), .sel(undriven));
  Multiplexer #(.width(2), .disabled(0), .enable("false")) multiplexer_15 (
    .in0(multiplexer_7_out), .in1(multiplexer_14_out), .out(multiplexer_15_out), .sel(undriven_2));
  Multiplexer #(.width(2), .enable("false")) multiplexer_16 (
    .in0(multiplexer_10_out), .in1(multiplexer_19_out), .out(multiplexer_16_out), .sel(undriven_2));
  Multiplexer #(.width(2), .enable("false")) multiplexer_17 (
    .in0(multiplexer_15_out), .in1(multiplexer_16_out), .out(multiplexer_17_out), .sel(undriven_3));
  Multiplexer #(.width(2), .disabled(0), .enable("false")) multiplexer_18 (
    .in0(undriven_7), .in1(undriven_11), .out(multiplexer_18_out), .sel(undriven));
  Multiplexer #(.width(2), .enable("false")) multiplexer_19 (
    .in0(undriven_6), .in1(undriven_10), .out(multiplexer_19_out), .sel(undriven));
  Multiplexer #(.width(2), .disabled(0), .enable("false")) multiplexer_20 (
    .in0(multiplexer_14_out), .in1(multiplexer_18_out), .out(multiplexer_20_out), .sel(undriven_2));
  Multiplexer #(.width(2), .disabled(0), .enable("false")) multiplexer_21 (
    .in0(multiplexer_16_out), .in1(multiplexer_20_out), .out(multiplexer_21_out), .sel(undriven_3));

  // Notes on the sheet:
  //   S4
  //   S2
  //   S1
  //   A7
  //   Y7
  //   A6
  //   Y6
  //   A5
  //   Y5
  //   A4
  //   Y4
  //   A3
  //   Y2
  //   Y3
  //   A2
  //   Y1
  //   A0
  //   A1
  //   Y0
endmodule
